// Logisim project ben_eater_602_logism.circ as structural Verilog: 1 circuit, main circuit main
module main (
  input  [7:0] DATA,
  output wr,
  output [15:0] ADDR
);

  wire button_1_out, w65c02s_pdip_40_1_p17, w65c02s_pdip_40_1_p19;

  // W65C02S__PDIP_40 w65c02s_pdip_40_1: pin names not known; wires that end beside it: 1'b1, 1'b1, 1'b1, 1'b1, ADDR[0], ADDR[1], ADDR[2], ADDR[3], ADDR[4], ADDR[5], ADDR[6], ADDR[7], ADDR[8], ADDR[9], ADDR[10], ADDR[11], w65c02s_pdip_40_1_p17, 1'b1, w65c02s_pdip_40_1_p19, 1'b1, wr, DATA[0], DATA[1], DATA[2], DATA[3], DATA[4], DATA[5], DATA[6], DATA[7], ADDR[15], ADDR[14], ADDR[13], ADDR[12], 1'b0, w65c02s_pdip_40_1_p19
  Clock #(.highDuration(2), .lowDuration(2)) clock_1 (.out(w65c02s_pdip_40_1_p19));
  Pull_Resistor #(.pull(1)) pull_resistor_1 (.node(w65c02s_pdip_40_1_p17));
  not not_1 (w65c02s_pdip_40_1_p17, button_1_out);
  Button button_1 (.out(button_1_out));
  ROM rom_1 ();  // open: addr, data
endmodule
